# Fritzing sketch Plane scheme (saved by Fritzing 0.9.5d)

parts:
  Компонент1 = Arduino Nano (Rev3.0)
  Power_plug1 = Power plug
  U1 = XD-RF-5V [package=THT]
  U2 = WS2812 RGB LED strip
  GY1 = MPU-6050 Board GY-521 [form="♀ (female)" package=THT]
  R1 = Resistor [tolerance=±5% resistance=220 package=THT]
  U3 = Voltage Regulator - 5V [package="TO220 [THT]"]
  Компонент2 = Triple Axis Accelerometer Breakout - ADXL335
  J7 = Basic Servo
  J8 = Basic Servo
  J9 = Basic Servo
  U4 = HC-SR04 [chip_label=IC package="SIP (Single Inline) [THT]"]
  J6 = Basic Servo
  J10 = Dagu DGServo 9g header connector (female) [package=THT]

nets:
  GND: Компонент1.GND, J6.gnd, J10.gnd
  N1: Компонент1.D2, U1.DATA
  N2: Компонент1.D3, U4.Trig, U4.Echo
  N3: Компонент1.D6, R1.Pin_0
  N4: Компонент1.D8, J6.pulse
  N5: Компонент1.D9, J7.pulse
  N6: Компонент1.D10, J8.pulse
  N7: Компонент1.D11/MOSI, J10.pulse
  5V: Компонент1.5V, U1.VCC
  N8: Компонент1.A5, GY1.pin3, Компонент2.YOUT
  N9: Компонент1.A4, GY1.pin4, Компонент2.XOUT
  GND_2: Power_plug1.GND, U2.GND, Компонент2.GND
  N10: Power_plug1.VCC, U3.input_voltage
  GND_3: U1.GND, U4.GND
  VCC: U2.VCC, U3.output_voltage, J9.vcc, J10.Vcc
  N11: U2.DIN, R1.Pin_1
  N12: GY1.pin1, Компонент2.VCC

notes:
  Подключен по I2C! Модель не точная

custom parts:
  XD-RF-5V: This is 433Mhz RF transmitter with receiver kit for Arduino ARM MCU wireless Application environment: Remote control switch, receiver module, motorcycles, automobile anti-theft products, home security products, electric doors, shutter doors, windows, remote control socket, remote control LED, remote audio remote control electric doors, garage door remote control, remote control retractable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
  WS2812 RGB LED strip: WS2812 strip
  MPU-6050 Board GY-521: Acelerometro y Giroscopio MPU-6050 Board GY-521
  HC-SR04: HC-SR04 ultrasound distance sensor
